# Fritzing sketch schema(components)-master (saved by Fritzing 1.0.2b)
circuit board: 11.0381cm x 8.6921cm

parts:
  U1 = ESP32-38PinWide [part_number=ESP32-38PinWide]
  ZS-042_RTC1 = ZS-042 RTC Module
  HC-1 = HC-12 Module
  Antenna1 = HC-12 Antenna
  LED1 = LED - 5mm [color="Red (633nm)" current=0.030A package="5 mm [THT]"]
  R1 = Resistor [tolerance=±5% power=0.25W resistance=1 package=THT]
  LCD1 = 2.8" SPI TFT Module [part_number=MSP2807]

nets:
  VCC: U1.3.3, ZS-042_RTC1.VCC, HC-1.VCC, LCD1.pin1
  N1: U1.GPIO32, HC-1.RXD
  N2: U1.GPIO33, HC-1.TXD
  N3: U1.GPIO14, LCD1.pin15
  N4: U1.GPIO12, LCD1.pin16
  N5: U1.GPIO13, LCD1.pin17
  N6: U1.GPIO11, HC-1.GND, LCD1.pin2
  N7: U1.GPIO15, LCD1.pin3
  N8: U1.GPIO2, LCD1.pin5
  N9: U1.GPIO0, R1.Pin_0
  N10: U1.GPIO4, LCD1.pin4
  N11: U1.GPIO16, LCD1.pin11
  N12: U1.GPIO17, LCD1.pin8, LCD1.pin10
  N13: U1.GPIO5, LCD1.pin18
  N14: U1.GPIO18, LCD1.pin7
  N15: U1.GPIO19, LCD1.pin13
  GND: U1.GND, ZS-042_RTC1.GND, LED1.cathode
  N16: U1.GPIO21, ZS-042_RTC1.SDA
  N17: U1.GPIO22, ZS-042_RTC1.SCL
  N18: U1.GPIO23, LCD1.pin6, LCD1.pin12
  N19: HC-1.ANT, Antenna1.ANT
  N20: LED1.anode, R1.Pin_1

custom parts:
  ESP32-38PinWide: Generic 38-Pin ESP32 with wide format (only access to one side of pins on a breadboard) based on Stephen Lilley's HiLetgo ESP-WROOM-32 ESP32 ESP-32S Development Board.
  HC-12 Module: HC-12 433Mhz Module
  HC-12 Antenna: Antenna for HC-12 433Mhz Module
  2.8" SPI TFT Module: A generic 2.8 inch LCD TFT 320x240 display with touchscreen and SD card slot. Uses the ILI9341 controller, like the Adafruit displays of this size uses.
