# Fritzing sketch schema(components)-slave (saved by Fritzing 1.0.2b)

parts:
  Part1 = Arduino Nano (Rev3.0) (ICSP)
  HC-1 = HC-12 Module
  Antenna1 = HC-12 Antenna
  LED1 = LED - 5mm [color="Red (633nm)" current=0.030A package="5 mm [THT]"]
  LED2 = LED - 5mm [color="Red (633nm)" current=0.030A package="5 mm [THT]"]
  LED3 = LED - 5mm [color="Red (633nm)" current=0.030A package="5 mm [THT]"]
  LED4 = LED - 5mm [color="Red (633nm)" current=0.030A package="5 mm [THT]"]
  R1 = Resistor [tolerance=±5% power=0.25W resistance=1 package=THT]
  R2 = Resistor [tolerance=±5% power=0.25W resistance=1 package=THT]
  R3 = Resistor [tolerance=±5% power=0.25W resistance=1 package=THT]
  R4 = Resistor [tolerance=±5% power=0.25W resistance=1 package=THT]

nets:
  GND: Part1.GND, HC-1.GND, LED1.cathode, LED2.cathode, LED3.cathode, LED4.cathode
  N1: Part1.D2, HC-1.RXD
  N2: Part1.D3, HC-1.TXD
  N3: Part1.D4, R1.Pin_1
  N4: Part1.D5, R2.Pin_1
  N5: Part1.D6, R3.Pin_1
  N6: Part1.D7, R4.Pin_1
  3V3: Part1.3V3, HC-1.VCC
  N7: HC-1.ANT, Antenna1.ANT
  N8: LED1.anode, R1.Pin_0
  N9: LED2.anode, R2.Pin_0
  N10: LED3.anode, R4.Pin_0
  N11: LED4.anode, R3.Pin_0

custom parts:
  HC-12 Module: HC-12 433Mhz Module
  HC-12 Antenna: Antenna for HC-12 433Mhz Module
